// Logisim project processor-surprise.circ as structural Verilog
module ALU (
  input  [2:0] F,
  input  [31:0] B,
  input  [31:0] A,
  output out_4,
  output [31:0] Y
);

  wire comparator_1_lt;
  wire [31:0] adder_1_out, adder_2_out, and_1_out, bit_extender_1_out, multiplier_1_out, multiplier_2_out,
       or_1_out;

  Adder #(.width(32)) adder_1 (.a(B), .b(A), .out(adder_1_out));  // open: cin, cout
  Adder #(.width(32)) adder_2 (.a(A), .b(multiplier_1_out), .out(adder_2_out));  // open: cin, cout
  Multiplier #(.width(32)) multiplier_1 (.a(B), .b({32{1'b1}}), .out(multiplier_1_out));  // open: cin, cout
  Comparator #(.width(32)) comparator_1 (.a(A), .b(B), .lt(comparator_1_lt));  // open: gt, eq
  assign and_1_out = B & A;  // AND_Gate and_1, 32 bits wide
  assign or_1_out = B | A;  // OR_Gate or_1, 32 bits wide
  Multiplier #(.width(32)) multiplier_2 (.a(A), .b(B), .out(multiplier_2_out));  // open: cin, cout
  assign bit_extender_1_out = {{31{1'b0}}, comparator_1_lt};  // Bit_Extender bit_extender_1
  Multiplexer #(.select(3), .width(32), .enable("false")) multiplexer_1 (
    .in0(and_1_out), .in1(or_1_out), .in2(adder_1_out), .in3(multiplier_2_out), .in6(adder_2_out),
    .in7(bit_extender_1_out), .out(Y), .sel(F));  // open: in4, in5
  Comparator #(.width(32), .mode("unsigned")) comparator_2 (.a({32{1'b0}}), .b(Y), .eq(out_4));  // open: gt, lt
endmodule

module Datapath (
  output [2:0] R2,
  output [2:0] R2_2,
  output [2:0] R2_3,
  output [31:0] v0,
  output [31:0] R1,
  output [31:0] R2_4,
  output [31:0] R2_5
);

  wire alu_1_out_4, and_1_out, clock_1_out, controlunit_1_alusrc, controlunit_1_branch, controlunit_1_regdst,
       controlunit_1_regwrite;
  wire [2:0] controlunit_1_alucontrol, multiplexer_1_out;
  wire [7:0] adder_1_out, adder_2_out, bitselector_5_out, multiplexer_3_out, register_1_q, shifter_1_out;
  wire [15:0] bitselector_4_out;
  wire [31:0] bit_extender_1_out, multiplexer_2_out, rom_1_data, shifter_2_out, shifter_3_out, shifter_4_out,
       shifter_5_out;

  Clock clock_1 (.out(clock_1_out));
  Register register_1 (.D(multiplexer_3_out), .Q(register_1_q), .clk(clock_1_out));  // open: en, clr
  Shifter #(.shift("lr")) shifter_1 (.in(register_1_q), .\dist (3'b010), .out(shifter_1_out));
  Adder adder_1 (.a(8'h4), .b(register_1_q), .out(adder_1_out));  // open: cin, cout
  ROM #(.dataWidth(32)) rom_1 (.addr(shifter_1_out), .data(rom_1_data));  // open: sel
  ControlUnit controlunit_1 (
    .Instruction(rom_1_data), .RegDst(controlunit_1_regdst), .RegWrite(controlunit_1_regwrite),
    .ALUControl(controlunit_1_alucontrol), .Branch(controlunit_1_branch), .ALUSrc(controlunit_1_alusrc));
  Shifter #(.width(32), .shift("lr")) shifter_2 (.in(rom_1_data), .\dist (5'b10101), .out(shifter_2_out));
  Shifter #(.width(32), .shift("lr")) shifter_3 (.in(rom_1_data), .\dist (5'b10000), .out(shifter_3_out));
  Shifter #(.width(32), .shift("lr")) shifter_4 (.in(rom_1_data), .\dist (5'b01011), .out(shifter_4_out));
  BitSelector #(.width(32), .group(3)) bitselector_1 (.in(shifter_2_out), .out(R2), .sel(4'b0000));
  BitSelector #(.width(32), .group(3)) bitselector_2 (.in(shifter_3_out), .out(R2_2), .sel(4'b0000));
  BitSelector #(.width(32), .group(3)) bitselector_3 (.in(shifter_4_out), .out(R2_3), .sel(4'b0000));
  Multiplexer #(.width(3), .enable("false")) multiplexer_1 (
    .in0(R2_2), .in1(R2_3), .out(multiplexer_1_out), .sel(controlunit_1_regdst));
  BitSelector #(.width(32), .group(16)) bitselector_4 (.in(rom_1_data), .out(bitselector_4_out), .sel(1'b0));
  RegisterFile registerfile_1 (
    .CLK(clock_1_out), .A1(R2), .WD3(R2_4), .A2(R2_2), .WE3(controlunit_1_regwrite), .RD1(R1), .RD2(R2_5),
    .A3(multiplexer_1_out), .V0(v0));
  assign bit_extender_1_out = {{16{bitselector_4_out[15]}}, bitselector_4_out};  // Bit_Extender bit_extender_1
  BitSelector #(.width(32), .group(8)) bitselector_5 (.in(shifter_5_out), .out(bitselector_5_out), .sel(2'b00));
  Shifter #(.width(32)) shifter_5 (.in(bit_extender_1_out), .\dist (5'b00010), .out(shifter_5_out));
  Multiplexer #(.width(32), .enable("false")) multiplexer_2 (
    .in0(R2_5), .in1(bit_extender_1_out), .out(multiplexer_2_out), .sel(controlunit_1_alusrc));
  ALU alu_1 (.F(controlunit_1_alucontrol), .B(multiplexer_2_out), .A(R1), .Y(R2_4), .out_4(alu_1_out_4));
  and and_1 (and_1_out, controlunit_1_branch, alu_1_out_4);
  Adder adder_2 (.a(adder_1_out), .b(bitselector_5_out), .out(adder_2_out));  // open: cin, cout
  Multiplexer #(.width(8), .enable("false")) multiplexer_3 (
    .in0(adder_1_out), .in1(adder_2_out), .out(multiplexer_3_out), .sel(and_1_out));

  // Notes on the sheet:
  //   contents of rom_1 (hex, n*v repeats v):
  //   20040004 20050000 20020001 10a40005 20 20a50001 70451002 1000fffb 20 1000ffff 20
endmodule

module Tests (
  output [31:0] Y,
  output [7:0] out_2,
  output [7:0] out_3,
  output [2:0] out_4
);

  BitSelector #(.width(32), .group(8)) bitselector_1 (.in(32'h12356789), .out(out_2), .sel(2'b01));
  BitSelector #(.width(32), .group(8)) bitselector_2 (.in(32'h12356789), .out(out_3), .sel(2'b01));
  BitSelector #(.group(3)) bitselector_3 (.in(out_3), .out(out_4), .sel(2'b00));

  assign Y = 32'hf4010207;

  // Notes on the sheet:
  //   binary values in Logisim. Convince yourself how the bits are displayed.
  //   Example 2: The bit selector is configured to have 32  
  //   bit group #1 (starting at index 0) is selected for the output.
  //   That is, the 8 bits 0x67 at bit indices 15..8  are sent to the output.
  //   Example 3: Now, assume that you want to extract 3 bits at   
  //   Example 1: A simple example that illustrates how 32-bit values are displayed as 
  //   input bits and 8 output bits. The parameter constant is 1, which means that   
  //   bit indices 10..8. This can be accoplished by putting two bit selecotrs in series.
endmodule

module RegisterFile (
  input  CLK,
  input  [2:0] A1,
  input  [31:0] WD3,
  input  [2:0] A2,
  input  WE3,
  input  [2:0] A3,
  output [31:0] RD1,
  output [31:0] RD2,
  output [31:0] V0
);

  wire and_1_out, and_2_out, and_3_out, and_4_out, and_5_out, and_6_out, and_7_out, decoder_1_out1,
       decoder_1_out2, decoder_1_out3, decoder_1_out4, decoder_1_out5, decoder_1_out6, decoder_1_out7;
  wire [31:0] bit_extender_1_out, register_1_q, register_3_q, register_4_q, register_5_q, register_6_q,
       register_7_q;

  Decoder #(.select(3)) decoder_1 (
    .out1(decoder_1_out1), .out2(decoder_1_out2), .out3(decoder_1_out3), .out4(decoder_1_out4),
    .out5(decoder_1_out5), .out6(decoder_1_out6), .out7(decoder_1_out7), .sel(A3));  // open: out0, en
  and and_1 (and_1_out, WE3, decoder_1_out1);
  and and_2 (and_2_out, WE3, decoder_1_out2);
  and and_3 (and_3_out, WE3, decoder_1_out3);
  and and_4 (and_4_out, WE3, decoder_1_out4);
  and and_5 (and_5_out, WE3, decoder_1_out5);
  and and_6 (and_6_out, WE3, decoder_1_out6);
  and and_7 (and_7_out, WE3, decoder_1_out7);
  Register #(.width(32)) register_1 (.D(WD3), .en(and_1_out), .Q(register_1_q), .clk(CLK));  // open: clr
  Register #(.width(32)) register_2 (.D(WD3), .en(and_2_out), .Q(V0), .clk(CLK));  // open: clr
  Register #(.width(32)) register_3 (.D(WD3), .en(and_3_out), .Q(register_3_q), .clk(CLK));  // open: clr
  Register #(.width(32)) register_4 (.D(WD3), .en(and_4_out), .Q(register_4_q), .clk(CLK));  // open: clr
  Register #(.width(32)) register_5 (.D(WD3), .en(and_5_out), .Q(register_5_q), .clk(CLK));  // open: clr
  Register #(.width(32)) register_6 (.D(WD3), .en(and_6_out), .Q(register_6_q), .clk(CLK));  // open: clr
  Register #(.width(32)) register_7 (.D(WD3), .en(and_7_out), .Q(register_7_q), .clk(CLK));  // open: clr
  assign bit_extender_1_out = {{31{1'b0}}, 1'b0};  // Bit_Extender bit_extender_1
  Multiplexer #(.select(3), .width(32)) multiplexer_1 (
    .in0(bit_extender_1_out), .in1(register_1_q), .in2(V0), .in3(register_3_q), .in4(register_4_q),
    .in5(register_5_q), .in6(register_6_q), .in7(register_7_q), .out(RD1), .sel(A1));  // open: en
  Multiplexer #(.select(3), .width(32)) multiplexer_2 (
    .in0(bit_extender_1_out), .in1(register_1_q), .in2(V0), .in3(register_3_q), .in4(register_4_q),
    .in5(register_5_q), .in6(register_6_q), .in7(register_7_q), .out(RD2), .sel(A2));  // open: en
endmodule

module ControlUnit (
  input  [31:0] Instruction,
  output RegDst,
  output RegWrite,
  output ALUSrc,
  output [2:0] ALUControl,
  output Branch
);

  wire comparator_2_eq;
  wire [1:1] comparator_4_eq;
  wire [5:0] bitselector_1_out;
  wire [31:0] shifter_1_out;

  Shifter #(.width(32), .shift("lr")) shifter_1 (.in(Instruction), .\dist (5'b11010), .out(shifter_1_out));
  BitSelector #(.width(32), .group(6)) bitselector_1 (.in(shifter_1_out), .out(bitselector_1_out), .sel(3'b000));
  Comparator #(.width(6), .mode("unsigned")) comparator_1 (
    .a(bitselector_1_out), .b(6'b001000), .eq(ALUSrc));  // open: gt, lt
  Comparator #(.width(6), .mode("unsigned")) comparator_2 (
    .a(bitselector_1_out), .b({6{1'b0}}), .eq(comparator_2_eq));  // open: gt, lt
  Comparator #(.width(6), .mode("unsigned")) comparator_3 (
    .a(bitselector_1_out), .b(6'b000100), .eq(Branch));  // open: gt, lt
  Comparator #(.width(6), .mode("unsigned")) comparator_4 (
    .a(bitselector_1_out), .b(6'b011100), .eq(comparator_4_eq[1]));  // open: gt, lt
  or or_1 (RegDst, comparator_2_eq, comparator_4_eq[1]);
  or or_2 (RegWrite, ALUSrc, comparator_4_eq[1], comparator_2_eq);
  Multiplexer #(.select(2), .width(3), .enable("false")) multiplexer_1 (
    .in0(3'b010), .in1(3'b110), .in2(3'b011), .out(ALUControl), .sel({comparator_4_eq[1], Branch}));  // open: in3

  // Notes on the sheet:
  //   0x2
  //   0x2
  //   0x6
  //   0x3
endmodule
