// Logisim project Module1.circ as structural Verilog: 1 circuit, main circuit main
module main (
);

  wire button_1_out, button_2_out, button_3_out, transistor_1_out, transistor_3_out, transistor_4_out,
       transistor_7_out;

  Button button_1 (.out(button_1_out));
  Button button_2 (.out(button_2_out));
  Button button_3 (.out(button_3_out));
  Transistor #(.\type ("n")) transistor_1 (.in(1'b0), .out(transistor_1_out), .gate(button_1_out));
  Transistor #(.\type ("n")) transistor_2 (.in(1'b0), .out(transistor_1_out), .gate(button_2_out));
  Transistor transistor_3 (.in(1'b1), .out(transistor_3_out), .gate(button_1_out));
  Transistor transistor_4 (.in(transistor_3_out), .out(transistor_4_out), .gate(button_2_out));
  Transistor transistor_5 (.in(transistor_4_out), .out(transistor_1_out), .gate(button_3_out));
  Transistor #(.\type ("n")) transistor_6 (.in(1'b0), .out(transistor_1_out), .gate(button_3_out));
  Transistor transistor_7 (.in(1'b1), .out(transistor_7_out), .gate(transistor_1_out));
  LED led_1 (.in(transistor_7_out));
  Transistor #(.\type ("n")) transistor_8 (.in(1'b0), .out(transistor_7_out), .gate(transistor_1_out));
endmodule
