// Logisim project Module2.circ as structural Verilog
module BirthdayModule (
  input  A,
  input  B,
  input  C,
  input  D,
  output Y
);

  wire and_1_out, and_2_out, and_3_out, not_1_out, not_2_out, not_3_out, not_4_out, not_5_out;

  not not_1 (not_1_out, B);
  and and_1 (and_1_out, not_1_out, not_2_out);
  not not_2 (not_2_out, D);
  not not_3 (not_3_out, A);
  and and_2 (and_2_out, not_3_out, not_4_out, C);
  not not_4 (not_4_out, B);
  and and_3 (and_3_out, B, not_5_out, D);
  not not_5 (not_5_out, C);
  or or_1 (Y, and_1_out, and_2_out, and_3_out);
endmodule
