// Logisim project Module3.circ as structural Verilog
module Module3FSM (
  input  A,
  input  B,
  input  q1,
  input  q0,
  output Q1_2,
  output Q0_2
);

  wire and_1_out, and_2_out, and_3_out, and_4_out, and_5_out, and_6_out, and_7_out, and_8_out, and_9_out,
       and_10_out, not_1_out, not_2_out, not_3_out, not_4_out, not_5_out, not_6_out, not_7_out, not_8_out,
       not_9_out, not_10_out, not_11_out, not_12_out, not_13_out, not_14_out, not_15_out, not_16_out;

  not not_1 (not_1_out, A);
  not not_2 (not_2_out, B);
  not not_3 (not_3_out, q1);
  not not_4 (not_4_out, A);
  not not_5 (not_5_out, q0);
  not not_6 (not_6_out, q1);
  not not_7 (not_7_out, B);
  not not_8 (not_8_out, q0);
  not not_9 (not_9_out, q1);
  not not_10 (not_10_out, A);
  not not_11 (not_11_out, q1);
  not not_12 (not_12_out, A);
  not not_13 (not_13_out, q0);
  not not_14 (not_14_out, B);
  not not_15 (not_15_out, q1);
  not not_16 (not_16_out, B);
  and and_1 (and_1_out, not_1_out, not_2_out, q1, q0);
  and and_2 (and_2_out, B, not_3_out, q0);
  and and_3 (and_3_out, not_4_out, B, q1, not_5_out);
  and and_4 (and_4_out, A, not_6_out, q0);
  and and_5 (and_5_out, A, not_7_out, q1, not_8_out);
  and and_6 (and_6_out, A, B, not_9_out);
  and and_7 (and_7_out, not_10_out, B, not_11_out, q0);
  and and_8 (and_8_out, not_12_out, B, q1, not_13_out);
  and and_9 (and_9_out, A, not_14_out, not_15_out);
  and and_10 (and_10_out, A, not_16_out, q0);
  or or_1 (Q1_2, and_1_out, and_2_out, and_3_out, and_4_out, and_5_out, and_6_out);
  or or_2 (Q0_2, and_7_out, and_8_out, and_9_out, and_10_out);
endmodule
